// Logisim project 01_Logic_gates.circ as structural Verilog: 1 circuit, main circuit Logic_gates
module Logic_gates (
  input  in_1,
  input  A,
  input  B,
  input  A_or,
  input  B_or,
  input  A_nand,
  input  B_nand,
  input  A_nor,
  input  B_nor,
  input  in_10,
  input  in_11,
  input  in_12,
  input  in_13,
  input  in_14,
  input  in_15,
  output out_16,
  output O,
  output O_or,
  output O_nand,
  output O_nor,
  output out_21,
  output out_22,
  output out_23
);

  wire and_1_out, and_2_out, and_3_out, and_4_out, not_1_out, not_2_out, not_3_out, not_4_out, xor_1_out;

  not not_1 (not_1_out, in_11);
  not not_2 (not_2_out, in_10);
  not not_3 (not_3_out, in_14);
  not not_4 (not_4_out, in_15);
  not not_5 (out_16, in_1);
  and and_1 (and_1_out, in_10, not_1_out);
  and and_2 (and_2_out, not_2_out, in_11);
  xor xor_1 (xor_1_out, in_12, in_13);
  not not_6 (out_22, xor_1_out);
  and and_3 (and_3_out, in_14, in_15);
  and and_4 (and_4_out, not_3_out, not_4_out);
  and and_5 (O, A, B);
  or or_1 (O_or, A_or, B_or);
  nand nand_1 (O_nand, A_nand, B_nand);
  nor nor_1 (O_nor, A_nor, B_nor);
  or or_2 (out_21, and_1_out, and_2_out);
  or or_3 (out_23, and_3_out, and_4_out);

  // Notes on the sheet:
  //   XOR Gate
  //   XNOR Gate
  //   NAND Gate
  //   NOR Gate
  //   NOT Gate
  //   AND Gate
  //   OR Gate
  //   XOR + NOT
endmodule
