// Logisim project 02_logic_gates_using_universal_gates.circ as structural Verilog: 1 circuit, main circuit main
module main (
  input  in_1,
  input  in_2,
  input  in_3,
  input  in_4,
  input  in_5,
  input  in_6,
  input  in_7,
  input  in_8,
  input  in_9,
  input  in_10,
  input  in_11,
  input  in_12,
  input  in_13,
  input  in_14,
  output out_15,
  output out_16,
  output out_17,
  output out_18,
  output out_19,
  output out_20,
  output out_21
);

  wire nand_1_out, nand_2_out, nand_3_out, nand_4_out, nand_5_out, nand_6_out, nand_7_out, nand_11_out,
       nand_12_out, nand_13_out, nor_1_out, nor_2_out, nor_3_out, nor_5_out, nor_6_out, nor_7_out;

  nand nand_1 (nand_1_out, in_6, in_6);
  nand nand_2 (nand_2_out, in_2, in_3);
  nand nand_3 (nand_3_out, in_8, in_8);
  nand nand_4 (nand_4_out, in_9, in_9);
  nand nand_5 (nand_5_out, in_12, in_12);
  nand nand_6 (nand_6_out, nand_4_out, in_12);
  nand nand_7 (nand_7_out, in_9, nand_5_out);
  nor nor_1 (nor_1_out, in_13, in_14);
  nand nand_8 (out_15, nand_2_out, nand_2_out);
  nand nand_9 (out_18, nand_1_out, nand_3_out);
  nor nor_2 (nor_2_out, nor_1_out, in_14);
  nand nand_10 (out_20, nand_6_out, nand_7_out);
  nor nor_3 (nor_3_out, in_13, nor_1_out);
  nor nor_4 (out_21, nor_3_out, nor_2_out);
  nor nor_5 (nor_5_out, in_1, in_1);
  nor nor_6 (nor_6_out, in_4, in_4);
  nor nor_7 (nor_7_out, in_5, in_7);
  nand nand_11 (nand_11_out, in_10, in_11);
  nor nor_8 (out_17, nor_7_out, nor_7_out);
  nand nand_12 (nand_12_out, in_10, nand_11_out);
  nand nand_13 (nand_13_out, nand_11_out, in_11);
  nor nor_9 (out_16, nor_5_out, nor_6_out);
  nand nand_14 (out_19, nand_12_out, nand_13_out);

  // Notes on the sheet:
  //   AND using NAND gates
  //   XOR using NAND (self attempt)
  //   OR using NAND
  //   XOR using NOR
  //   AND using NOR gates
  //   XOR using NAND (logical one)
  //   OR using NOR gates
endmodule
