// Logisim project 03_Half_and_full_adders.circ as structural Verilog: 3 circuits, main circuit adders
module adders (
  input  A,
  input  in_2,
  input  B,
  input  in_4,
  input  Cin,
  input  in_6,
  input  in_7,
  input  in_8,
  input  in_9,
  input  in_10,
  output out_11,
  output Sum,
  output out_13,
  output Carry,
  output out_15,
  output out_16,
  output out_17,
  output out_18
);

  wire and_2_out, and_3_out, and_4_out, and_5_out, nand_1_out, nand_3_out, nand_4_out, or_1_out, xor_2_out,
       xor_3_out;

  nand nand_1 (nand_1_out, in_6, in_9);
  nand nand_2 (out_17, nand_1_out, nand_1_out);
  xor xor_1 (out_11, in_2, in_4);
  and and_1 (out_13, in_2, in_4);
  nand nand_3 (nand_3_out, in_6, nand_1_out);
  nand nand_4 (nand_4_out, nand_1_out, in_9);
  nand nand_5 (out_15, nand_3_out, nand_4_out);
  and and_2 (and_2_out, A, B);
  or or_1 (or_1_out, A, B);
  xor xor_2 (xor_2_out, A, B);
  xor xor_3 (xor_3_out, in_7, in_8);
  and and_3 (and_3_out, in_7, in_8);
  xor xor_4 (Sum, xor_2_out, Cin);
  and and_4 (and_4_out, Cin, or_1_out);
  or or_2 (Carry, and_2_out, and_4_out);
  xor xor_5 (out_16, xor_3_out, in_10);
  and and_5 (and_5_out, xor_3_out, in_10);
  or or_3 (out_18, and_5_out, and_3_out);

  // Notes on the sheet:
  //   Half Adder
  //   Half Adder Using NAND only
  //   A XOR B
  //   A.B
  //   A+B
  //   Full Adder (self attempt)
  //   A XOR B XOR C
  //   C.(A+B) = AC+BC
  //   A XOR B
  //   A.B (Carry_1)
  //   Full adder using Gates
  //   A xor B xor C
  //   Carry 2
  //   Carry1 + Carry 2
endmodule

module Half_adder (
  input  in_1,
  input  in_2,
  output out_3,
  output out_4
);

  wire nand_1_out, nand_3_out, nand_4_out;

  nand nand_1 (nand_1_out, in_1, in_2);
  nand nand_2 (out_4, nand_1_out, nand_1_out);
  nand nand_3 (nand_3_out, in_1, nand_1_out);
  nand nand_4 (nand_4_out, nand_1_out, in_2);
  nand nand_5 (out_3, nand_3_out, nand_4_out);
endmodule

module Full_adder_using_half_adder (
  input  in_1,
  input  in_2,
  input  in_3,
  output out_4,
  output out_5
);

  wire half_adder_1_out_3, half_adder_1_out_4, half_adder_2_out_4;

  Half_adder half_adder_1 (.in_1(in_1), .in_2(in_2), .out_3(half_adder_1_out_3), .out_4(half_adder_1_out_4));
  Half_adder half_adder_2 (.in_1(half_adder_1_out_3), .in_2(in_3), .out_3(out_4), .out_4(half_adder_2_out_4));
  or or_1 (out_5, half_adder_2_out_4, half_adder_1_out_4);

  // Notes on the sheet:
  //   Full Adder using Half Adder
endmodule
